// Logisim project CPU.circ as structural Verilog
module main (
);

  wire and_1_out, button_1_out, button_2_out, comparator_1_eq, cpu_1_out_10, cpu_1_writemem, gpu_1_out_5,
       gpu_1_out_6, gpu_1_out_7, gpu_1_out_8, gpu_1_out_9, gpu_1_out_10, gpu_1_out_11, gpu_1_out_12;
  wire [3:0] gpu_1_out_3, gpu_1_out_4;
  wire [6:0] cpu_1_screen;
  wire [15:0] cpu_1_out_5, cpu_1_out_6;
  wire [31:0] cpu_1_out_8, gregs_1_out_5, gregs_1_out_6, gregs_1_out_7, gregs_1_out_8, gregs_1_out_9,
       gregs_1_out_10, gregs_1_out_11, gregs_1_out_12, gregs_1_out_13, gregs_1_out_14, gregs_1_out_15,
       gregs_1_out_16, gregs_1_out_17, gregs_1_out_18, gregs_1_out_19, gregs_1_out_20, gregs_2_out_5,
       gregs_2_out_6, gregs_2_out_7, gregs_2_out_8, gregs_2_out_9, gregs_2_out_10, gregs_2_out_11,
       gregs_2_out_12, gregs_2_out_13, gregs_2_out_14, gregs_2_out_15, gregs_2_out_16, gregs_2_out_17,
       gregs_2_out_18, gregs_2_out_19, gregs_2_out_20, gregs_3_out_5, gregs_3_out_6, gregs_3_out_7,
       gregs_3_out_8, gregs_3_out_9, gregs_3_out_10, gregs_3_out_11, gregs_3_out_12, gregs_3_out_13,
       gregs_3_out_14, gregs_3_out_15, gregs_3_out_16, gregs_3_out_17, gregs_3_out_18, gregs_3_out_19,
       gregs_3_out_20, gregs_4_out_5, gregs_4_out_6, gregs_4_out_7, gregs_4_out_8, gregs_4_out_9,
       gregs_4_out_10, gregs_4_out_11, gregs_4_out_12, gregs_4_out_13, gregs_4_out_14, gregs_4_out_15,
       gregs_4_out_16, gregs_4_out_17, gregs_4_out_18, gregs_4_out_19, gregs_4_out_20, gregs_5_out_5,
       gregs_5_out_6, gregs_5_out_7, gregs_5_out_8, gregs_5_out_9, gregs_5_out_10, gregs_5_out_11,
       gregs_5_out_12, gregs_5_out_13, gregs_5_out_14, gregs_5_out_15, gregs_5_out_16, gregs_5_out_17,
       gregs_5_out_18, gregs_5_out_19, gregs_5_out_20, gregs_6_out_5, gregs_6_out_6, gregs_6_out_7,
       gregs_6_out_8, gregs_6_out_9, gregs_6_out_10, gregs_6_out_11, gregs_6_out_12, gregs_6_out_13,
       gregs_6_out_14, gregs_6_out_15, gregs_6_out_16, gregs_6_out_17, gregs_6_out_18, gregs_6_out_19,
       gregs_6_out_20, gregs_7_out_5, gregs_7_out_6, gregs_7_out_7, gregs_7_out_8, gregs_7_out_9,
       gregs_7_out_10, gregs_7_out_11, gregs_7_out_12, gregs_7_out_13, gregs_7_out_14, gregs_7_out_15,
       gregs_7_out_16, gregs_7_out_17, gregs_7_out_18, gregs_7_out_19, gregs_7_out_20, gregs_8_out_5,
       gregs_8_out_6, gregs_8_out_7, gregs_8_out_8, gregs_8_out_9, gregs_8_out_10, gregs_8_out_11,
       gregs_8_out_12, gregs_8_out_13, gregs_8_out_14, gregs_8_out_15, gregs_8_out_16, gregs_8_out_17,
       gregs_8_out_18, gregs_8_out_19, gregs_8_out_20, ram_1_data, rom_1_data;

  Button button_1 (.out(button_1_out));
  Button button_2 (.out(button_2_out));
  CPU cpu_1 (
    .in_1(button_1_out), .out_5(cpu_1_out_5), .in_2(rom_1_data), .in_3(button_2_out), .RAM_in(ram_1_data),
    .writemem(cpu_1_writemem), .out_8(cpu_1_out_8), .out_6(cpu_1_out_6), .SCREEN(cpu_1_screen),
    .out_10(cpu_1_out_10));
  ROM #(.addrWidth(16), .dataWidth(32)) rom_1 (.addr(cpu_1_out_5), .data(rom_1_data));  // open: sel
  Comparator #(.width(16)) comparator_1 (.a({16{1'b0}}), .b(cpu_1_out_6), .eq(comparator_1_eq));  // open: gt, lt
  RAM #(.addrWidth(16), .dataWidth(32), .bus("separate")) ram_1 (
    .addr(cpu_1_out_6), .din(cpu_1_out_8), .data(ram_1_data), .str(cpu_1_writemem), .clk(cpu_1_writemem),
    .ld(cpu_1_out_10), .clr(button_2_out));  // open: sel
  and and_1 (and_1_out, comparator_1_eq, cpu_1_writemem);
  gpu gpu_1 (
    .in_1(cpu_1_screen), .in_2(and_1_out), .out_3(gpu_1_out_3), .out_4(gpu_1_out_4), .out_5(gpu_1_out_5),
    .out_6(gpu_1_out_6), .out_7(gpu_1_out_7), .out_8(gpu_1_out_8), .out_9(gpu_1_out_9),
    .out_10(gpu_1_out_10), .out_11(gpu_1_out_11), .out_12(gpu_1_out_12));
  DotMatrix #(.inputtype("row"), .matrixcols(32), .matrixrows(32)) dotmatrix_1 (
    .row0(gregs_1_out_5), .row1(gregs_1_out_6), .row2(gregs_1_out_7), .row3(gregs_1_out_8),
    .row4(gregs_1_out_9), .row5(gregs_1_out_10), .row6(gregs_1_out_11), .row7(gregs_1_out_12),
    .row8(gregs_1_out_13), .row9(gregs_1_out_14), .row10(gregs_1_out_15), .row11(gregs_1_out_16),
    .row12(gregs_1_out_17), .row13(gregs_1_out_18), .row14(gregs_1_out_19), .row15(gregs_1_out_20),
    .row16(gregs_2_out_5), .row17(gregs_2_out_6), .row18(gregs_2_out_7), .row19(gregs_2_out_8),
    .row20(gregs_2_out_9), .row21(gregs_2_out_10), .row22(gregs_2_out_11), .row23(gregs_2_out_12),
    .row24(gregs_2_out_13), .row25(gregs_2_out_14), .row26(gregs_2_out_15), .row27(gregs_2_out_16),
    .row28(gregs_2_out_17), .row29(gregs_2_out_18), .row30(gregs_2_out_19), .row31(gregs_2_out_20));
  gregs gregs_1 (
    .in_2(cpu_1_out_8), .in_3(gpu_1_out_3), .out_5(gregs_1_out_5), .out_6(gregs_1_out_6),
    .out_7(gregs_1_out_7), .out_8(gregs_1_out_8), .out_9(gregs_1_out_9), .out_10(gregs_1_out_10),
    .out_11(gregs_1_out_11), .out_12(gregs_1_out_12), .out_13(gregs_1_out_13), .out_14(gregs_1_out_14),
    .out_15(gregs_1_out_15), .out_16(gregs_1_out_16), .out_17(gregs_1_out_17), .out_18(gregs_1_out_18),
    .out_19(gregs_1_out_19), .out_20(gregs_1_out_20), .in_4(gpu_1_out_5), .in_1(button_2_out));
  gregs gregs_2 (
    .in_2(cpu_1_out_8), .in_3(gpu_1_out_3), .out_5(gregs_2_out_5), .out_6(gregs_2_out_6),
    .out_7(gregs_2_out_7), .out_8(gregs_2_out_8), .out_9(gregs_2_out_9), .out_10(gregs_2_out_10),
    .out_11(gregs_2_out_11), .out_12(gregs_2_out_12), .out_13(gregs_2_out_13), .out_14(gregs_2_out_14),
    .out_15(gregs_2_out_15), .out_16(gregs_2_out_16), .out_17(gregs_2_out_17), .out_18(gregs_2_out_18),
    .out_19(gregs_2_out_19), .out_20(gregs_2_out_20), .in_4(gpu_1_out_6), .in_1(button_2_out));
  DotMatrix #(.inputtype("row"), .matrixcols(32), .matrixrows(32)) dotmatrix_2 (
    .row0(gregs_3_out_5), .row1(gregs_3_out_6), .row2(gregs_3_out_7), .row3(gregs_3_out_8),
    .row4(gregs_3_out_9), .row5(gregs_3_out_10), .row6(gregs_3_out_11), .row7(gregs_3_out_12),
    .row8(gregs_3_out_13), .row9(gregs_3_out_14), .row10(gregs_3_out_15), .row11(gregs_3_out_16),
    .row12(gregs_3_out_17), .row13(gregs_3_out_18), .row14(gregs_3_out_19), .row15(gregs_3_out_20),
    .row16(gregs_4_out_5), .row17(gregs_4_out_6), .row18(gregs_4_out_7), .row19(gregs_4_out_8),
    .row20(gregs_4_out_9), .row21(gregs_4_out_10), .row22(gregs_4_out_11), .row23(gregs_4_out_12),
    .row24(gregs_4_out_13), .row25(gregs_4_out_14), .row26(gregs_4_out_15), .row27(gregs_4_out_16),
    .row28(gregs_4_out_17), .row29(gregs_4_out_18), .row30(gregs_4_out_19), .row31(gregs_4_out_20));
  gregs gregs_3 (
    .in_2(cpu_1_out_8), .in_3(gpu_1_out_3), .out_5(gregs_3_out_5), .out_6(gregs_3_out_6),
    .out_7(gregs_3_out_7), .out_8(gregs_3_out_8), .out_9(gregs_3_out_9), .out_10(gregs_3_out_10),
    .out_11(gregs_3_out_11), .out_12(gregs_3_out_12), .out_13(gregs_3_out_13), .out_14(gregs_3_out_14),
    .out_15(gregs_3_out_15), .out_16(gregs_3_out_16), .out_17(gregs_3_out_17), .out_18(gregs_3_out_18),
    .out_19(gregs_3_out_19), .out_20(gregs_3_out_20), .in_4(gpu_1_out_7), .in_1(button_2_out));
  gregs gregs_4 (
    .in_2(cpu_1_out_8), .in_3(gpu_1_out_3), .out_5(gregs_4_out_5), .out_6(gregs_4_out_6),
    .out_7(gregs_4_out_7), .out_8(gregs_4_out_8), .out_9(gregs_4_out_9), .out_10(gregs_4_out_10),
    .out_11(gregs_4_out_11), .out_12(gregs_4_out_12), .out_13(gregs_4_out_13), .out_14(gregs_4_out_14),
    .out_15(gregs_4_out_15), .out_16(gregs_4_out_16), .out_17(gregs_4_out_17), .out_18(gregs_4_out_18),
    .out_19(gregs_4_out_19), .out_20(gregs_4_out_20), .in_4(gpu_1_out_8), .in_1(button_2_out));
  DotMatrix #(.inputtype("row"), .matrixcols(32), .matrixrows(32)) dotmatrix_3 (
    .row0(gregs_5_out_20), .row1(gregs_5_out_19), .row2(gregs_5_out_18), .row3(gregs_5_out_17),
    .row4(gregs_5_out_16), .row5(gregs_5_out_15), .row6(gregs_5_out_14), .row7(gregs_5_out_13),
    .row8(gregs_5_out_12), .row9(gregs_5_out_11), .row10(gregs_5_out_10), .row11(gregs_5_out_9),
    .row12(gregs_5_out_8), .row13(gregs_5_out_7), .row14(gregs_5_out_6), .row15(gregs_5_out_5),
    .row16(gregs_6_out_20), .row17(gregs_6_out_19), .row18(gregs_6_out_18), .row19(gregs_6_out_17),
    .row20(gregs_6_out_16), .row21(gregs_6_out_15), .row22(gregs_6_out_14), .row23(gregs_6_out_13),
    .row24(gregs_6_out_12), .row25(gregs_6_out_11), .row26(gregs_6_out_10), .row27(gregs_6_out_9),
    .row28(gregs_6_out_8), .row29(gregs_6_out_7), .row30(gregs_6_out_6), .row31(gregs_6_out_5));
  DotMatrix #(.inputtype("row"), .matrixcols(32), .matrixrows(32)) dotmatrix_4 (
    .row0(gregs_7_out_20), .row1(gregs_7_out_19), .row2(gregs_7_out_18), .row3(gregs_7_out_17),
    .row4(gregs_7_out_16), .row5(gregs_7_out_15), .row6(gregs_7_out_14), .row7(gregs_7_out_13),
    .row8(gregs_7_out_12), .row9(gregs_7_out_11), .row10(gregs_7_out_10), .row11(gregs_7_out_9),
    .row12(gregs_7_out_8), .row13(gregs_7_out_7), .row14(gregs_7_out_6), .row15(gregs_7_out_5),
    .row16(gregs_8_out_20), .row17(gregs_8_out_19), .row18(gregs_8_out_18), .row19(gregs_8_out_17),
    .row20(gregs_8_out_16), .row21(gregs_8_out_15), .row22(gregs_8_out_14), .row23(gregs_8_out_13),
    .row24(gregs_8_out_12), .row25(gregs_8_out_11), .row26(gregs_8_out_10), .row27(gregs_8_out_9),
    .row28(gregs_8_out_8), .row29(gregs_8_out_7), .row30(gregs_8_out_6), .row31(gregs_8_out_5));
  gregs gregs_5 (
    .in_2(cpu_1_out_8), .in_3(gpu_1_out_4), .out_5(gregs_5_out_5), .out_6(gregs_5_out_6),
    .out_7(gregs_5_out_7), .out_8(gregs_5_out_8), .out_9(gregs_5_out_9), .out_10(gregs_5_out_10),
    .out_11(gregs_5_out_11), .out_12(gregs_5_out_12), .out_13(gregs_5_out_13), .out_14(gregs_5_out_14),
    .out_15(gregs_5_out_15), .out_16(gregs_5_out_16), .out_17(gregs_5_out_17), .out_18(gregs_5_out_18),
    .out_19(gregs_5_out_19), .out_20(gregs_5_out_20), .in_4(gpu_1_out_9), .in_1(button_2_out));
  gregs gregs_6 (
    .in_2(cpu_1_out_8), .in_3(gpu_1_out_4), .out_5(gregs_6_out_5), .out_6(gregs_6_out_6),
    .out_7(gregs_6_out_7), .out_8(gregs_6_out_8), .out_9(gregs_6_out_9), .out_10(gregs_6_out_10),
    .out_11(gregs_6_out_11), .out_12(gregs_6_out_12), .out_13(gregs_6_out_13), .out_14(gregs_6_out_14),
    .out_15(gregs_6_out_15), .out_16(gregs_6_out_16), .out_17(gregs_6_out_17), .out_18(gregs_6_out_18),
    .out_19(gregs_6_out_19), .out_20(gregs_6_out_20), .in_4(gpu_1_out_10), .in_1(button_2_out));
  gregs gregs_7 (
    .in_2(cpu_1_out_8), .in_3(gpu_1_out_4), .out_5(gregs_7_out_5), .out_6(gregs_7_out_6),
    .out_7(gregs_7_out_7), .out_8(gregs_7_out_8), .out_9(gregs_7_out_9), .out_10(gregs_7_out_10),
    .out_11(gregs_7_out_11), .out_12(gregs_7_out_12), .out_13(gregs_7_out_13), .out_14(gregs_7_out_14),
    .out_15(gregs_7_out_15), .out_16(gregs_7_out_16), .out_17(gregs_7_out_17), .out_18(gregs_7_out_18),
    .out_19(gregs_7_out_19), .out_20(gregs_7_out_20), .in_4(gpu_1_out_11), .in_1(button_2_out));
  gregs gregs_8 (
    .in_2(cpu_1_out_8), .in_3(gpu_1_out_4), .out_5(gregs_8_out_5), .out_6(gregs_8_out_6),
    .out_7(gregs_8_out_7), .out_8(gregs_8_out_8), .out_9(gregs_8_out_9), .out_10(gregs_8_out_10),
    .out_11(gregs_8_out_11), .out_12(gregs_8_out_12), .out_13(gregs_8_out_13), .out_14(gregs_8_out_14),
    .out_15(gregs_8_out_15), .out_16(gregs_8_out_16), .out_17(gregs_8_out_17), .out_18(gregs_8_out_18),
    .out_19(gregs_8_out_19), .out_20(gregs_8_out_20), .in_4(gpu_1_out_12), .in_1(button_2_out));

  // Notes on the sheet:
  //   on/off
  //   rst
  //   ROM
  //   contents of rom_1 (hex, n*v repeats v):
  //   8000047 20270000 20480000 e84825 49290006 11200001 ca00000 30e9001f 30ea0020 200c0001 14c5004
  //   1485025 200b001f 1694822 1896804 8d4e0001 1cd7025 ad4e0001 454a0010 ad4e0000 ca00000 23382a 10070003
  //   614022 20090001 10000002 234022 28090001 44382a 10070003 825022 200b0001 10000002 445022 280b0001
  //   148382a 10070002 490c0001 10000002 494c0001 c6022 acc50005 20050031 acc80000 acc90001 acca0002
  //   accb0003 accc0004 8000001 233822 448022 2073825 14070002 8cc50005 ca00000 8ccc0004 8ccb0003 8cca0002
  //   8cc90001 8cc80000 c6820 1a87020 e382a 10070002 18a6022 290820 1aa382a 10070002 1886020 4b1020
  //   1000ffe4 200600c8 20010014 20020019 20030028 2004003c 2005004e 8000015 20010014 20020019 20030034
  //   2004001e 20050054 8000015 20010028 2002003c 20030034 2004001e 2005005a 8000015
endmodule

module CPU (
  input  in_1,
  input  [31:0] in_2,
  input  in_3,
  input  [31:0] RAM_in,
  output [15:0] out_5,
  output [15:0] out_6,
  output [6:0] SCREEN,
  output [31:0] out_8,
  output writemem,
  output out_10
);

  wire bneq_1_x, clock_1_out_2, clock_1_out_3, clock_1_out_4, clock_1_out_5, comparator_1_eq, decoder_1_out1,
       id_1_beq, id_1_bne, id_1_out_6, id_1_out_7, id_1_out_9, id_1_out_10, id_1_out_12, not_1_out,
       not_2_out, or_1_out, or_2_out, or_3_out, or_4_out;
  wire [1:0] id_1_out_5;
  wire [3:0] id_1_out_15;
  wire [4:0] id_1_rd, id_1_rs, id_1_rt;
  wire [15:0] id_1_out_14, multiplexer_1_out, pc_1_out_6, register_1_q;
  wire [31:0] alu_1_out_4, bit_extender_1_out, bit_extender_2_out, multiplexer_2_out, multiplexer_3_out,
       multiplexer_4_out, register_2_q, register_4_q, regs_1_out_7, regs_1_out_8;
  wire [31:23] multiplexer_5_out;

  clock clock_1 (
    .in_1(in_1), .out_2(clock_1_out_2), .out_3(clock_1_out_3), .out_4(clock_1_out_4), .out_5(clock_1_out_5));
  ID id_1 (
    .in_1(in_2), .clk(clock_1_out_5), .rst(or_1_out), .rd(id_1_rd), .rs(id_1_rs), .rt(id_1_rt),
    .out_14(id_1_out_14), .out_15(id_1_out_15), .out_9(id_1_out_9), .out_5(id_1_out_5[0]),
    .out_10(id_1_out_10), .out_12(id_1_out_12), .beq(id_1_beq), .bne(id_1_bne), .out_6(id_1_out_6),
    .out_7(id_1_out_7));  // open: out_8
  or or_1 (or_1_out, in_1, in_3);
  or or_2 (or_2_out, id_1_out_9, id_1_out_5[0]);
  Decoder #(.disabled(0)) decoder_1 (.out1(decoder_1_out1), .sel(or_2_out), .en(clock_1_out_4));  // open: out0
  D d_1 (.a(clock_1_out_3), .b(id_1_out_10), .c(id_1_out_12), .x(out_10), .y(writemem));
  or or_3 (or_3_out, id_1_out_12, id_1_out_10);
  or or_4 (or_4_out, id_1_bne, id_1_beq);
  Bneq bneq_1 (.a(id_1_bne), .x(bneq_1_x), .b(id_1_beq), .c(not_2_out));
  not not_1 (not_1_out, or_4_out);
  not not_2 (not_2_out, comparator_1_eq);
  or or_5 (id_1_out_5[1], bneq_1_x, id_1_out_7);
  PC pc_1 (
    .in_1(multiplexer_1_out), .MEM_BRANCH(clock_1_out_3), .out_7(out_5), .in_2(or_1_out), .IF(clock_1_out_5),
    .out_6(pc_1_out_6), .stop(id_1_out_6));
  Register #(.width(16)) register_1 (
    .D(id_1_out_14), .en(1'b1), .Q(register_1_q), .clk(decoder_1_out1), .clr(or_1_out));
  Regs regs_1 (
    .RS(id_1_rs), .IN(id_1_rd), .RT(id_1_rt), .RST(clock_1_out_2), .in_5(multiplexer_4_out), .CLK(or_1_out),
    .out_7(regs_1_out_7), .out_8(regs_1_out_8));
  assign bit_extender_1_out = {{16{1'b0}}, register_1_q};  // Bit_Extender bit_extender_1
  Multiplexer #(.select(2), .width(16)) multiplexer_1 (
    .in0(pc_1_out_6), .in1(register_1_q), .in2(alu_1_out_4[15:0]), .out(multiplexer_1_out), .sel(id_1_out_5),
    .en(1'b1));  // open: in3
  assign bit_extender_2_out = {{16{1'b0}}, pc_1_out_6};  // Bit_Extender bit_extender_2
  Comparator #(.width(32)) comparator_1 (.a(regs_1_out_8), .b(regs_1_out_7), .eq(comparator_1_eq));  // open: gt, lt
  Register #(.width(32)) register_2 (
    .D(regs_1_out_7), .en(1'b1), .Q(register_2_q), .clk(clock_1_out_4), .clr(or_1_out));
  Register #(.width(32)) register_3 (.D(regs_1_out_8), .en(1'b1), .Q(out_8), .clk(clock_1_out_4), .clr(or_1_out));
  Register #(.width(32), .trigger("high")) register_4 (
    .D(RAM_in), .en(1'b1), .Q(register_4_q), .clk(out_10), .clr(or_1_out));
  ALU alu_1 (.in_1(multiplexer_2_out), .in_3(multiplexer_3_out), .out_4(alu_1_out_4), .control(id_1_out_15));
  Multiplexer #(.width(32)) multiplexer_2 (
    .in0(bit_extender_2_out), .in1(register_2_q), .out(multiplexer_2_out), .sel(not_1_out), .en(1'b1));
  Multiplexer #(.width(32)) multiplexer_3 (
    .in0(out_8), .in1(bit_extender_1_out), .out(multiplexer_3_out), .sel(id_1_out_9), .en(1'b1));
  Multiplexer #(.width(32)) multiplexer_4 (
    .in0(alu_1_out_4), .in1(register_4_q), .out(multiplexer_4_out), .sel(id_1_out_10), .en(1'b1));
  Multiplexer #(.width(32), .disabled(0)) multiplexer_5 (
    .in1(alu_1_out_4), .out({multiplexer_5_out, SCREEN, out_6}), .sel(or_3_out), .en(or_3_out));  // open: in0

  // Notes on the sheet:
  //   PC+4/J/b
  //   LW
  //   imm
  //   A
  //   B
  //   LMD
  //   RAMout
  //   MEMAddr
endmodule

module ALU (
  input  [31:0] in_1,
  input  [3:0] control,
  input  [31:0] in_3,
  output [31:0] out_4
);

  wire [31:0] adder_1_out, and_1_out, bit_extender_1_out, divider_1_out, divider_1_rem, multiplier_1_out,
       or_1_out, shifter_1_out, shifter_2_out, subtractor_1_out, subtractor_2_out, xor_1_out;

  Adder #(.width(32)) adder_1 (.a(in_1), .b(in_3), .out(adder_1_out));  // open: cin, cout
  Subtractor #(.width(32)) subtractor_1 (.a(in_1), .b(in_3), .out(subtractor_1_out));  // open: bin, bout
  Multiplier #(.width(32)) multiplier_1 (.a(in_1), .b(in_3), .out(multiplier_1_out));  // open: cin, cout
  Divider #(.width(32)) divider_1 (.a(in_1), .b(in_3), .out(divider_1_out), .rem(divider_1_rem));  // open: upper
  assign and_1_out = in_1 & in_3;  // AND_Gate and_1, 32 bits wide
  assign or_1_out = in_1 | in_3;  // OR_Gate or_1, 32 bits wide
  assign xor_1_out = in_1 ^ in_3;  // XOR_Gate xor_1, 32 bits wide
  Subtractor #(.width(32)) subtractor_2 (.a(in_1), .b(in_3), .out(subtractor_2_out));  // open: bin, bout
  Shifter #(.width(32)) shifter_1 (.in(in_1), .\dist (in_3[4:0]), .out(shifter_1_out));
  Shifter #(.width(32), .shift("lr")) shifter_2 (.in(in_1), .\dist (in_3[4:0]), .out(shifter_2_out));
  assign bit_extender_1_out = {{31{1'b0}}, subtractor_2_out[31]};  // Bit_Extender bit_extender_1
  Multiplexer #(.select(4), .width(32)) multiplexer_1 (
    .in0(adder_1_out), .in1(subtractor_1_out), .in2(bit_extender_1_out), .in3(multiplier_1_out),
    .in4(divider_1_out), .in5(divider_1_rem), .in6(and_1_out), .in7(or_1_out), .in8(xor_1_out),
    .in9(shifter_1_out), .in10(shifter_2_out), .out(out_4), .sel(control), .en(1'b1));  // open: in11, in12, in13, in14, in15

  // Notes on the sheet:
  //   A
  //   B
  //   ALUo
endmodule

module Regs (
  input  [4:0] RS,
  input  [4:0] IN,
  input  [4:0] RT,
  input  RST,
  input  [31:0] in_5,
  input  CLK,
  output [31:0] out_7,
  output [31:0] out_8
);

  wire decoder_1_out1, decoder_1_out2, decoder_1_out3, decoder_1_out4, decoder_1_out5, decoder_1_out6,
       decoder_1_out7, decoder_1_out8, decoder_1_out9, decoder_1_out10, decoder_1_out11, decoder_1_out12,
       decoder_1_out13, decoder_1_out14, decoder_1_out15, decoder_1_out16, decoder_1_out17, decoder_1_out18,
       decoder_1_out19, decoder_1_out20, decoder_1_out21, decoder_1_out22, decoder_1_out23, decoder_1_out24,
       decoder_1_out25, decoder_1_out26, decoder_1_out27, decoder_1_out28, decoder_1_out29, decoder_1_out30,
       decoder_1_out31;
  wire [31:0] register_1_q, register_2_q, register_3_q, register_4_q, register_5_q, register_6_q,
       register_7_q, register_8_q, register_9_q, register_10_q, register_11_q, register_12_q, register_13_q,
       register_14_q, register_15_q, register_16_q, register_17_q, register_18_q, register_19_q,
       register_20_q, register_21_q, register_22_q, register_23_q, register_24_q, register_25_q,
       register_26_q, register_27_q, register_28_q, register_29_q, register_30_q, register_31_q,
       register_32_q;

  Decoder #(.select(5), .disabled(0)) decoder_1 (
    .out1(decoder_1_out1), .out2(decoder_1_out2), .out3(decoder_1_out3), .out4(decoder_1_out4),
    .out5(decoder_1_out5), .out6(decoder_1_out6), .out7(decoder_1_out7), .out8(decoder_1_out8),
    .out9(decoder_1_out9), .out10(decoder_1_out10), .out11(decoder_1_out11), .out12(decoder_1_out12),
    .out13(decoder_1_out13), .out14(decoder_1_out14), .out15(decoder_1_out15), .out16(decoder_1_out16),
    .out17(decoder_1_out17), .out18(decoder_1_out18), .out19(decoder_1_out19), .out20(decoder_1_out20),
    .out21(decoder_1_out21), .out22(decoder_1_out22), .out23(decoder_1_out23), .out24(decoder_1_out24),
    .out25(decoder_1_out25), .out26(decoder_1_out26), .out27(decoder_1_out27), .out28(decoder_1_out28),
    .out29(decoder_1_out29), .out30(decoder_1_out30), .out31(decoder_1_out31), .sel(IN), .en(1'b1));  // open: out0
  Register #(.width(32)) register_1 (.D(in_5), .en(decoder_1_out31), .Q(register_1_q), .clk(RST), .clr(CLK));
  Register #(.width(32)) register_2 (.D(in_5), .en(decoder_1_out30), .Q(register_2_q), .clk(RST), .clr(CLK));
  Register #(.width(32)) register_3 (.D(in_5), .en(decoder_1_out29), .Q(register_3_q), .clk(RST), .clr(CLK));
  Register #(.width(32)) register_4 (.D(in_5), .en(decoder_1_out28), .Q(register_4_q), .clk(RST), .clr(CLK));
  Register #(.width(32)) register_5 (.D(in_5), .en(decoder_1_out27), .Q(register_5_q), .clk(RST), .clr(CLK));
  Register #(.width(32)) register_6 (.D(in_5), .en(decoder_1_out26), .Q(register_6_q), .clk(RST), .clr(CLK));
  Register #(.width(32)) register_7 (.D(in_5), .en(decoder_1_out25), .Q(register_7_q), .clk(RST), .clr(CLK));
  Register #(.width(32)) register_8 (.D(in_5), .en(decoder_1_out24), .Q(register_8_q), .clk(RST), .clr(CLK));
  Register #(.width(32)) register_9 (.D(in_5), .en(decoder_1_out23), .Q(register_9_q), .clk(RST), .clr(CLK));
  Register #(.width(32)) register_10 (.D(in_5), .en(decoder_1_out22), .Q(register_10_q), .clk(RST), .clr(CLK));
  Register #(.width(32)) register_11 (.D(in_5), .en(decoder_1_out21), .Q(register_11_q), .clk(RST), .clr(CLK));
  Register #(.width(32)) register_12 (.D(in_5), .en(decoder_1_out20), .Q(register_12_q), .clk(RST), .clr(CLK));
  Register #(.width(32)) register_13 (.D(in_5), .en(decoder_1_out19), .Q(register_13_q), .clk(RST), .clr(CLK));
  Register #(.width(32)) register_14 (.D(in_5), .en(decoder_1_out18), .Q(register_14_q), .clk(RST), .clr(CLK));
  Register #(.width(32)) register_15 (.D(in_5), .en(decoder_1_out17), .Q(register_15_q), .clk(RST), .clr(CLK));
  Register #(.width(32)) register_16 (.D(in_5), .en(decoder_1_out16), .Q(register_16_q), .clk(RST), .clr(CLK));
  Register #(.width(32)) register_17 (.D(in_5), .en(decoder_1_out15), .Q(register_17_q), .clk(RST), .clr(CLK));
  Register #(.width(32)) register_18 (.D(in_5), .en(decoder_1_out14), .Q(register_18_q), .clk(RST), .clr(CLK));
  Register #(.width(32)) register_19 (.D(in_5), .en(decoder_1_out13), .Q(register_19_q), .clk(RST), .clr(CLK));
  Register #(.width(32)) register_20 (.D(in_5), .en(decoder_1_out12), .Q(register_20_q), .clk(RST), .clr(CLK));
  Register #(.width(32)) register_21 (.D(in_5), .en(decoder_1_out11), .Q(register_21_q), .clk(RST), .clr(CLK));
  Register #(.width(32)) register_22 (.D(in_5), .en(decoder_1_out10), .Q(register_22_q), .clk(RST), .clr(CLK));
  Register #(.width(32)) register_23 (.D(in_5), .en(decoder_1_out9), .Q(register_23_q), .clk(RST), .clr(CLK));
  Register #(.width(32)) register_24 (.D(in_5), .en(decoder_1_out8), .Q(register_24_q), .clk(RST), .clr(CLK));
  Register #(.width(32)) register_25 (.D(in_5), .en(decoder_1_out7), .Q(register_25_q), .clk(RST), .clr(CLK));
  Register #(.width(32)) register_26 (.D(in_5), .en(decoder_1_out6), .Q(register_26_q), .clk(RST), .clr(CLK));
  Register #(.width(32)) register_27 (.D(in_5), .en(decoder_1_out5), .Q(register_27_q), .clk(RST), .clr(CLK));
  Register #(.width(32)) register_28 (.D(in_5), .en(decoder_1_out4), .Q(register_28_q), .clk(RST), .clr(CLK));
  Register #(.width(32)) register_29 (.D(in_5), .en(decoder_1_out3), .Q(register_29_q), .clk(RST), .clr(CLK));
  Register #(.width(32)) register_30 (.D(in_5), .en(decoder_1_out2), .Q(register_30_q), .clk(RST), .clr(CLK));
  Register #(.width(32)) register_31 (.D(in_5), .en(decoder_1_out1), .Q(register_31_q), .clk(RST), .clr(CLK));
  Register #(.width(32)) register_32 (.D(in_5), .en(1'b0), .Q(register_32_q), .clk(RST), .clr(CLK));
  Multiplexer #(.select(5), .width(32)) multiplexer_1 (
    .in0(register_32_q), .in1(register_31_q), .in2(register_30_q), .in3(register_29_q), .in4(register_28_q),
    .in5(register_27_q), .in6(register_26_q), .in7(register_25_q), .in8(register_24_q), .in9(register_23_q),
    .in10(register_22_q), .in11(register_21_q), .in12(register_20_q), .in13(register_19_q),
    .in14(register_18_q), .in15(register_17_q), .in16(register_16_q), .in17(register_15_q),
    .in18(register_14_q), .in19(register_13_q), .in20(register_12_q), .in21(register_11_q),
    .in22(register_10_q), .in23(register_9_q), .in24(register_8_q), .in25(register_7_q), .in26(register_6_q),
    .in27(register_5_q), .in28(register_4_q), .in29(register_3_q), .in30(register_2_q), .in31(register_1_q),
    .out(out_7), .sel(RS), .en(1'b1));
  Multiplexer #(.select(5), .width(32)) multiplexer_2 (
    .in0(register_32_q), .in1(register_31_q), .in2(register_30_q), .in3(register_29_q), .in4(register_28_q),
    .in5(register_27_q), .in6(register_26_q), .in7(register_25_q), .in8(register_24_q), .in9(register_23_q),
    .in10(register_22_q), .in11(register_21_q), .in12(register_20_q), .in13(register_19_q),
    .in14(register_18_q), .in15(register_17_q), .in16(register_16_q), .in17(register_15_q),
    .in18(register_14_q), .in19(register_13_q), .in20(register_12_q), .in21(register_11_q),
    .in22(register_10_q), .in23(register_9_q), .in24(register_8_q), .in25(register_7_q), .in26(register_6_q),
    .in27(register_5_q), .in28(register_4_q), .in29(register_3_q), .in30(register_2_q), .in31(register_1_q),
    .out(out_8), .sel(RT), .en(1'b1));

  // Notes on the sheet:
  //   DATA IN
  //   31
  //   23
  //   15
  //   7
  //   0
  //   A
  //   B
endmodule

module PC (
  input  [15:0] in_1,
  input  in_2,
  input  IF,
  input  MEM_BRANCH,
  input  stop,
  output [15:0] out_6,
  output [15:0] out_7
);

  wire [15:0] adder_1_out, multiplexer_1_out;

  Register #(.width(16)) register_1 (.D(in_1), .en(1'b1), .Q(out_7), .clk(MEM_BRANCH), .clr(in_2));
  Multiplexer #(.width(16), .enable("false")) multiplexer_1 (
    .in0(16'h1), .in1({16{1'b0}}), .out(multiplexer_1_out), .sel(stop));
  Adder #(.width(16)) adder_1 (.a(out_7), .b(multiplexer_1_out), .out(adder_1_out));  // open: cin, cout
  Register #(.width(16)) register_2 (.D(adder_1_out), .en(1'b1), .Q(out_6), .clk(IF), .clr(in_2));

  // Notes on the sheet:
  //   add
  //   PC
  //   NPC
  //   npco
  //   PC
endmodule

module ID (
  input  [31:0] in_1,
  input  clk,
  input  rst,
  output [4:0] rd,
  output out_5,
  output out_6,
  output out_7,
  output out_8,
  output out_9,
  output out_10,
  output [4:0] rs,
  output out_12,
  output [4:0] rt,
  output [15:0] out_14,
  output [3:0] out_15,
  output beq,
  output bne
);

  wire de_in_id_1_u, de_in_id_1_z, not_1_out, not_2_out, or_1_out;
  wire [31:26] register_1_q;

  Comparator #(.width(32)) comparator_1 (.a(in_1), .b({32{1'b0}}), .eq(out_6));  // open: gt, lt
  Register #(.width(32)) register_1 (.D(in_1), .en(1'b1), .Q({register_1_q, rs, rt, out_14}), .clk(clk), .clr(rst));
  Demultiplexer #(.disabled(0), .enable("false")) demultiplexer_1 (
    .out0(out_5), .out1(out_7), .in(de_in_id_1_z), .sel(register_1_q[26]));
  DE_in_ID de_in_id_1 (
    .a(register_1_q[31]), .b(register_1_q[30]), .x(out_8), .c(register_1_q[29]), .d(register_1_q[28]),
    .e(register_1_q[27]), .f(register_1_q[26]), .y(out_9), .z(de_in_id_1_z), .u(de_in_id_1_u), .v(out_10),
    .w(out_12));
  FuncDecode funcdecode_1 (.in_1(out_14[5:0]), .in_2(register_1_q), .in_3(out_9), .out_4(out_15));
  Multiplexer #(.width(5), .disabled(0)) multiplexer_1 (
    .in0(out_14[15:11]), .in1(rt), .out(rd), .sel(not_1_out), .en(not_2_out));
  not not_1 (not_1_out, out_8);
  not not_2 (not_2_out, or_1_out);
  or or_1 (or_1_out, out_12, de_in_id_1_u);
  Decoder #(.disabled(0)) decoder_1 (.out0(beq), .out1(bne), .sel(register_1_q[26]), .en(de_in_id_1_u));

  // Notes on the sheet:
  //   instruction
  //   IR
  //   imm
endmodule

module DE_in_ID (
  input  a,
  input  b,
  input  c,
  input  d,
  input  e,
  input  f,
  output x,
  output y,
  output z,
  output u,
  output v,
  output w
);

  wire and_2_out, and_3_out, and_4_out, and_5_out, and_6_out, and_7_out, and_8_out, not_1_out, not_2_out,
       not_3_out, not_4_out, not_5_out, not_6_out, not_7_out, not_8_out, not_9_out, not_10_out, not_11_out,
       not_12_out, not_13_out, not_14_out, not_15_out, not_16_out, not_17_out, not_18_out, not_19_out,
       not_20_out, not_21_out, not_22_out, not_23_out, not_24_out, not_25_out, not_26_out, not_27_out,
       not_28_out, not_29_out, not_30_out, not_31_out, not_32_out, not_33_out, not_34_out, not_35_out,
       not_36_out, not_37_out, not_38_out, not_39_out;

  not not_1 (not_1_out, a);
  not not_2 (not_2_out, b);
  not not_3 (not_3_out, c);
  not not_4 (not_4_out, d);
  not not_5 (not_5_out, e);
  not not_6 (not_6_out, f);
  not not_7 (not_7_out, a);
  not not_8 (not_8_out, b);
  not not_9 (not_9_out, e);
  not not_10 (not_10_out, a);
  not not_11 (not_11_out, b);
  not not_12 (not_12_out, f);
  not not_13 (not_13_out, a);
  not not_14 (not_14_out, d);
  not not_15 (not_15_out, f);
  not not_16 (not_16_out, a);
  not not_17 (not_17_out, c);
  not not_18 (not_18_out, d);
  not not_19 (not_19_out, e);
  not not_20 (not_20_out, a);
  not not_21 (not_21_out, d);
  not not_22 (not_22_out, f);
  not not_23 (not_23_out, a);
  not not_24 (not_24_out, d);
  not not_25 (not_25_out, b);
  not not_26 (not_26_out, d);
  not not_27 (not_27_out, a);
  not not_28 (not_28_out, b);
  not not_29 (not_29_out, c);
  not not_30 (not_30_out, d);
  not not_31 (not_31_out, a);
  not not_32 (not_32_out, b);
  not not_33 (not_33_out, c);
  not not_34 (not_34_out, e);
  not not_35 (not_35_out, b);
  not not_36 (not_36_out, c);
  not not_37 (not_37_out, d);
  not not_38 (not_38_out, b);
  not not_39 (not_39_out, d);
  and and_1 (x, not_1_out, not_2_out, not_3_out, not_4_out, not_5_out, not_6_out);
  and and_2 (and_2_out, not_7_out, not_8_out, d, not_9_out);
  and and_3 (and_3_out, not_10_out, not_11_out, c, not_12_out);
  and and_4 (and_4_out, not_13_out, c, not_14_out, not_15_out);
  and and_5 (and_5_out, not_16_out, b, not_17_out, not_18_out, not_19_out, f);
  and and_6 (and_6_out, not_20_out, b, not_21_out, e, not_22_out);
  and and_7 (and_7_out, not_23_out, b, c, not_24_out, e);
  and and_8 (and_8_out, a, not_25_out, not_26_out, e, f);
  and and_9 (z, not_27_out, not_28_out, not_29_out, not_30_out, e);
  and and_10 (u, not_31_out, not_32_out, not_33_out, d, not_34_out);
  and and_11 (v, a, not_35_out, not_36_out, not_37_out, e, f);
  and and_12 (w, a, not_38_out, c, not_39_out, e, f);
  or or_1 (y, and_2_out, and_3_out, and_4_out, and_5_out, and_6_out, and_7_out, and_8_out);
endmodule

module FuncDecode (
  input  [5:0] in_1,
  input  [5:0] in_2,
  input  in_3,
  output [3:0] out_4
);

  wire [3:0] fd1_1_u, fd2_1_u;

  fd1 fd1_1 (
    .a(in_1[5]), .b(in_1[4]), .c(in_1[3]), .d(in_1[2]), .e(in_1[1]), .f(in_1[0]), .x(fd1_1_u[3]),
    .y(fd1_1_u[2]), .z(fd1_1_u[1]), .u(fd1_1_u[0]));
  fd2 fd2_1 (
    .a(in_2[5]), .b(in_2[4]), .c(in_2[3]), .d(in_2[2]), .e(in_2[1]), .f(in_2[0]), .x(fd2_1_u[3]),
    .y(fd2_1_u[2]), .z(fd2_1_u[1]), .u(fd2_1_u[0]));
  Multiplexer #(.width(4), .disabled(0)) multiplexer_1 (
    .in0(fd1_1_u), .in1(fd2_1_u), .out(out_4), .sel(in_3), .en(1'b1));
endmodule

module fd1 (
  input  a,
  input  b,
  input  c,
  input  d,
  input  e,
  input  f,
  output x,
  output y,
  output z,
  output u
);

  wire and_1_out, and_2_out, and_3_out, and_4_out, and_5_out, and_6_out, and_7_out, and_8_out, and_9_out,
       and_10_out, and_11_out, and_12_out, and_13_out, not_1_out, not_2_out, not_3_out, not_4_out, not_5_out,
       not_6_out, not_7_out, not_8_out, not_9_out, not_10_out, not_11_out, not_12_out, not_13_out,
       not_14_out, not_15_out, not_16_out, not_17_out, not_18_out, not_19_out, not_20_out, not_21_out,
       not_22_out, not_23_out, not_24_out, not_25_out, not_26_out, not_27_out, not_28_out, not_29_out,
       not_30_out, not_31_out, not_32_out, not_33_out, not_34_out, not_35_out, not_36_out, not_37_out,
       not_38_out, not_39_out, not_40_out, not_41_out, not_42_out, not_43_out, not_44_out;

  not not_1 (not_1_out, a);
  not not_2 (not_2_out, b);
  not not_3 (not_3_out, c);
  not not_4 (not_4_out, f);
  not not_5 (not_5_out, b);
  not not_6 (not_6_out, c);
  not not_7 (not_7_out, f);
  not not_8 (not_8_out, b);
  not not_9 (not_9_out, c);
  not not_10 (not_10_out, e);
  not not_11 (not_11_out, c);
  not not_12 (not_12_out, d);
  not not_13 (not_13_out, a);
  not not_14 (not_14_out, b);
  not not_15 (not_15_out, c);
  not not_16 (not_16_out, f);
  not not_17 (not_17_out, b);
  not not_18 (not_18_out, c);
  not not_19 (not_19_out, e);
  not not_20 (not_20_out, b);
  not not_21 (not_21_out, d);
  not not_22 (not_22_out, f);
  not not_23 (not_23_out, c);
  not not_24 (not_24_out, d);
  not not_25 (not_25_out, e);
  not not_26 (not_26_out, f);
  not not_27 (not_27_out, a);
  not not_28 (not_28_out, b);
  not not_29 (not_29_out, c);
  not not_30 (not_30_out, e);
  not not_31 (not_31_out, f);
  not not_32 (not_32_out, b);
  not not_33 (not_33_out, c);
  not not_34 (not_34_out, d);
  not not_35 (not_35_out, f);
  not not_36 (not_36_out, b);
  not not_37 (not_37_out, c);
  not not_38 (not_38_out, e);
  not not_39 (not_39_out, c);
  not not_40 (not_40_out, d);
  not not_41 (not_41_out, e);
  not not_42 (not_42_out, f);
  not not_43 (not_43_out, c);
  not not_44 (not_44_out, d);
  and and_1 (and_1_out, not_1_out, not_2_out, not_3_out, d, not_4_out);
  and and_2 (and_2_out, not_5_out, not_6_out, d, e, not_7_out);
  and and_3 (and_3_out, a, not_8_out, not_9_out, d, not_10_out);
  and and_4 (and_4_out, a, b, not_11_out, not_12_out, e);
  and and_5 (and_5_out, not_13_out, not_14_out, not_15_out, d, e, not_16_out);
  and and_6 (and_6_out, a, not_17_out, not_18_out, d, not_19_out);
  and and_7 (and_7_out, a, not_20_out, c, not_21_out, e, not_22_out);
  and and_8 (and_8_out, a, b, not_23_out, not_24_out, not_25_out, not_26_out);
  and and_9 (and_9_out, not_27_out, not_28_out, not_29_out, d, not_30_out, not_31_out);
  and and_10 (and_10_out, a, not_32_out, not_33_out, not_34_out, e, not_35_out);
  and and_11 (and_11_out, a, not_36_out, not_37_out, d, not_38_out, f);
  and and_12 (and_12_out, a, b, not_39_out, not_40_out, not_41_out, not_42_out);
  and and_13 (and_13_out, a, b, not_43_out, not_44_out, e, f);
  or or_1 (x, and_1_out, and_2_out);
  or or_2 (y, and_3_out, and_4_out);
  or or_3 (z, and_5_out, and_6_out, and_7_out, and_8_out);
  or or_4 (u, and_9_out, and_10_out, and_11_out, and_12_out, and_13_out);
endmodule

module fd2 (
  input  a,
  input  b,
  input  c,
  input  d,
  input  e,
  input  f,
  output x,
  output y,
  output z,
  output u
);

  wire and_1_out, and_2_out, and_3_out, and_4_out, and_5_out, and_6_out, and_7_out, and_8_out, and_9_out,
       and_10_out, and_11_out, and_12_out, and_13_out, not_1_out, not_2_out, not_3_out, not_4_out, not_5_out,
       not_6_out, not_7_out, not_8_out, not_9_out, not_10_out, not_11_out, not_12_out, not_13_out,
       not_14_out, not_15_out, not_16_out, not_17_out, not_18_out, not_19_out, not_20_out, not_21_out,
       not_22_out, not_23_out, not_24_out, not_25_out, not_26_out, not_27_out, not_28_out, not_29_out,
       not_30_out, not_31_out, not_32_out, not_33_out, not_34_out, not_35_out, not_36_out, not_37_out,
       not_38_out, not_39_out, not_40_out, not_41_out, not_42_out, not_43_out, not_44_out;

  not not_1 (not_1_out, a);
  not not_2 (not_2_out, b);
  not not_3 (not_3_out, f);
  not not_4 (not_4_out, a);
  not not_5 (not_5_out, c);
  not not_6 (not_6_out, d);
  not not_7 (not_7_out, e);
  not not_8 (not_8_out, a);
  not not_9 (not_9_out, c);
  not not_10 (not_10_out, d);
  not not_11 (not_11_out, f);
  not not_12 (not_12_out, a);
  not not_13 (not_13_out, b);
  not not_14 (not_14_out, e);
  not not_15 (not_15_out, a);
  not not_16 (not_16_out, d);
  not not_17 (not_17_out, a);
  not not_18 (not_18_out, b);
  not not_19 (not_19_out, e);
  not not_20 (not_20_out, a);
  not not_21 (not_21_out, c);
  not not_22 (not_22_out, d);
  not not_23 (not_23_out, f);
  not not_24 (not_24_out, a);
  not not_25 (not_25_out, d);
  not not_26 (not_26_out, e);
  not not_27 (not_27_out, f);
  not not_28 (not_28_out, a);
  not not_29 (not_29_out, b);
  not not_30 (not_30_out, d);
  not not_31 (not_31_out, f);
  not not_32 (not_32_out, a);
  not not_33 (not_33_out, b);
  not not_34 (not_34_out, e);
  not not_35 (not_35_out, a);
  not not_36 (not_36_out, c);
  not not_37 (not_37_out, d);
  not not_38 (not_38_out, e);
  not not_39 (not_39_out, a);
  not not_40 (not_40_out, d);
  not not_41 (not_41_out, e);
  not not_42 (not_42_out, f);
  not not_43 (not_43_out, a);
  not not_44 (not_44_out, d);
  and and_1 (and_1_out, not_1_out, not_2_out, c, d, e, not_3_out);
  and and_2 (and_2_out, not_4_out, b, not_5_out, not_6_out, not_7_out, f);
  and and_3 (and_3_out, not_8_out, b, not_9_out, not_10_out, e, not_11_out);
  and and_4 (and_4_out, not_12_out, not_13_out, c, d, not_14_out);
  and and_5 (and_5_out, not_15_out, b, c, not_16_out, e);
  and and_6 (and_6_out, not_17_out, not_18_out, c, d, not_19_out);
  and and_7 (and_7_out, not_20_out, b, not_21_out, not_22_out, e, not_23_out);
  and and_8 (and_8_out, not_24_out, b, c, not_25_out, not_26_out, not_27_out);
  and and_9 (and_9_out, not_28_out, not_29_out, c, not_30_out, e, not_31_out);
  and and_10 (and_10_out, not_32_out, not_33_out, c, d, not_34_out, f);
  and and_11 (and_11_out, not_35_out, b, not_36_out, not_37_out, not_38_out, f);
  and and_12 (and_12_out, not_39_out, b, c, not_40_out, not_41_out, not_42_out);
  and and_13 (and_13_out, not_43_out, b, c, not_44_out, e, f);
  or or_1 (x, and_1_out, and_2_out, and_3_out);
  or or_2 (y, and_4_out, and_5_out);
  or or_3 (z, and_6_out, and_7_out, and_8_out);
  or or_4 (u, and_9_out, and_10_out, and_11_out, and_12_out, and_13_out);
endmodule

module D (
  input  a,
  input  b,
  input  c,
  output x,
  output y
);

  wire not_1_out, not_2_out;

  not not_1 (not_1_out, c);
  not not_2 (not_2_out, b);
  and and_1 (x, a, b, not_1_out);
  and and_2 (y, a, not_2_out, c);
endmodule

module clock (
  input  in_1,
  output out_2,
  output out_3,
  output out_4,
  output out_5
);

  wire clock_1_out, shift_register_1_out, shift_register_1_q3, t_ff_1_q;

  Clock clock_1 (.out(clock_1_out));
  T_Flip_Flop t_ff_1 (.clk(in_1), .T(1'b1), .Q(t_ff_1_q), .en(1'b1));  // open: Qn, preset, reset
  Shift_Register #(.length(4)) shift_register_1 (
    .shift(t_ff_1_q), .in(shift_register_1_out), .clk(clock_1_out), .out(shift_register_1_out), .load(in_1),
    .d0(1'b0), .q0(out_5), .d1(1'b0), .q1(out_4), .d2(1'b0), .q2(out_3), .d3(1'b1), .q3(shift_register_1_q3));  // open: clr
  and and_1 (out_2, shift_register_1_q3, t_ff_1_q);
endmodule

module Bneq (
  input  a,
  input  b,
  input  c,
  output x
);

  wire and_1_out, and_2_out, not_1_out, not_2_out, not_3_out;

  not not_1 (not_1_out, a);
  not not_2 (not_2_out, c);
  not not_3 (not_3_out, b);
  and and_1 (and_1_out, not_1_out, b, not_2_out);
  and and_2 (and_2_out, a, not_3_out, c);
  or or_1 (x, and_1_out, and_2_out);
endmodule

module gpu (
  input  [6:0] in_1,
  input  in_2,
  output [3:0] out_3,
  output [3:0] out_4,
  output out_5,
  output out_6,
  output out_7,
  output out_8,
  output out_9,
  output out_10,
  output out_11,
  output out_12
);

  Decoder #(.select(3), .disabled(0)) decoder_1 (
    .out0(out_5), .out1(out_6), .out2(out_7), .out3(out_8), .out4(out_9), .out5(out_10), .out6(out_11),
    .out7(out_12), .sel(in_1[6:4]), .en(in_2));
  Subtractor #(.width(4)) subtractor_1 (.a(4'b1111), .b(in_1[3:0]), .out(out_4));  // open: bin, bout

  assign out_3 = in_1[3:0];
endmodule

module gregs (
  input  in_1,
  input  [31:0] in_2,
  input  [3:0] in_3,
  input  in_4,
  output [31:0] out_5,
  output [31:0] out_6,
  output [31:0] out_7,
  output [31:0] out_8,
  output [31:0] out_9,
  output [31:0] out_10,
  output [31:0] out_11,
  output [31:0] out_12,
  output [31:0] out_13,
  output [31:0] out_14,
  output [31:0] out_15,
  output [31:0] out_16,
  output [31:0] out_17,
  output [31:0] out_18,
  output [31:0] out_19,
  output [31:0] out_20
);

  wire decoder_1_out0, decoder_1_out1, decoder_1_out2, decoder_1_out3, decoder_1_out4, decoder_1_out5,
       decoder_1_out6, decoder_1_out7, decoder_1_out8, decoder_1_out9, decoder_1_out10, decoder_1_out11,
       decoder_1_out12, decoder_1_out13, decoder_1_out14, decoder_1_out15;

  Decoder #(.select(4), .disabled(0)) decoder_1 (
    .out0(decoder_1_out0), .out1(decoder_1_out1), .out2(decoder_1_out2), .out3(decoder_1_out3),
    .out4(decoder_1_out4), .out5(decoder_1_out5), .out6(decoder_1_out6), .out7(decoder_1_out7),
    .out8(decoder_1_out8), .out9(decoder_1_out9), .out10(decoder_1_out10), .out11(decoder_1_out11),
    .out12(decoder_1_out12), .out13(decoder_1_out13), .out14(decoder_1_out14), .out15(decoder_1_out15),
    .sel(in_3), .en(in_4));
  Register #(.width(32)) register_1 (.D(in_2), .en(decoder_1_out0), .Q(out_5), .clk(decoder_1_out0), .clr(in_1));
  Register #(.width(32)) register_2 (.D(in_2), .en(decoder_1_out4), .Q(out_9), .clk(decoder_1_out4), .clr(in_1));
  Register #(.width(32)) register_3 (.D(in_2), .en(decoder_1_out8), .Q(out_13), .clk(decoder_1_out8), .clr(in_1));
  Register #(.width(32)) register_4 (.D(in_2), .en(decoder_1_out12), .Q(out_17), .clk(decoder_1_out12), .clr(in_1));
  Register #(.width(32)) register_5 (.D(in_2), .en(decoder_1_out1), .Q(out_6), .clk(decoder_1_out1), .clr(in_1));
  Register #(.width(32)) register_6 (.D(in_2), .en(decoder_1_out5), .Q(out_10), .clk(decoder_1_out5), .clr(in_1));
  Register #(.width(32)) register_7 (.D(in_2), .en(decoder_1_out9), .Q(out_14), .clk(decoder_1_out9), .clr(in_1));
  Register #(.width(32)) register_8 (.D(in_2), .en(decoder_1_out13), .Q(out_18), .clk(decoder_1_out13), .clr(in_1));
  Register #(.width(32)) register_9 (.D(in_2), .en(decoder_1_out2), .Q(out_7), .clk(decoder_1_out2), .clr(in_1));
  Register #(.width(32)) register_10 (.D(in_2), .en(decoder_1_out6), .Q(out_11), .clk(decoder_1_out6), .clr(in_1));
  Register #(.width(32)) register_11 (.D(in_2), .en(decoder_1_out10), .Q(out_15), .clk(decoder_1_out10), .clr(in_1));
  Register #(.width(32)) register_12 (.D(in_2), .en(decoder_1_out14), .Q(out_19), .clk(decoder_1_out14), .clr(in_1));
  Register #(.width(32)) register_13 (.D(in_2), .en(decoder_1_out3), .Q(out_8), .clk(decoder_1_out3), .clr(in_1));
  Register #(.width(32)) register_14 (.D(in_2), .en(decoder_1_out7), .Q(out_12), .clk(decoder_1_out7), .clr(in_1));
  Register #(.width(32)) register_15 (.D(in_2), .en(decoder_1_out11), .Q(out_16), .clk(decoder_1_out11), .clr(in_1));
  Register #(.width(32)) register_16 (.D(in_2), .en(decoder_1_out15), .Q(out_20), .clk(decoder_1_out15), .clr(in_1));
endmodule
